// Logisim project 150115048_150114048_150114016.circ as structural Verilog: 23 circuits, main circuit D_Latch
// D
module D_Latch (
  input  D,
  input  WE,
  input  AscSet0,
  output Output
);

  wire and_1_out, and_2_out, nor_1_out;

  and and_1 (and_1_out, D, WE);
  and and_2 (and_2_out, WE, ~D);  // AND_Gate
  Pull_Resistor pull_resistor_1 (.node(AscSet0));
  nor nor_1 (nor_1_out, and_1_out, Output);
  nor nor_2 (Output, nor_1_out, AscSet0, and_2_out);
endmodule

module D_Flip_Flop (
  input  WE,
  input  \input ,
  input  clock,
  input  AscSet0,
  output \output 
);

  wire d_latch_2_output, multiplexer_1_out, not_1_out;

  Pull_Resistor pull_resistor_1 (.node(AscSet0));
  Pull_Resistor #(.pull(1)) pull_resistor_2 (.node(WE));
  Multiplexer #(.enable("false")) multiplexer_1 (.in0(\output ), .in1(\input ), .out(multiplexer_1_out), .sel(WE));
  not not_1 (not_1_out, clock);
  D_Latch d_latch_1 (.WE(clock), .D(d_latch_2_output), .Output(\output ), .AscSet0(AscSet0));
  D_Latch d_latch_2 (.WE(not_1_out), .D(multiplexer_1_out), .Output(d_latch_2_output), .AscSet0(AscSet0));
endmodule

// 1bitDec
module _1BitDecoder (
  input  Bit,
  input  Enable,
  output _0,
  output _1
);

  wire not_1_out;

  Pull_Resistor #(.pull(1)) pull_resistor_1 (.node(Enable));
  not not_1 (not_1_out, Bit);
  and and_1 (_0, not_1_out, Enable);
  and and_2 (_1, Bit, Enable);
endmodule

// 2bitDec
module _2BitDecoder (
  input  [1:0] Input,
  input  Enable,
  output [3:0] \output 
);

  wire n1bitdecoder_1__0, n1bitdecoder_1__1;

  _1BitDecoder u_1bitdecoder_1 (._0(n1bitdecoder_1__0), ._1(n1bitdecoder_1__1), .Bit(Input[1]), .Enable(Enable));
  Pull_Resistor #(.pull(1)) pull_resistor_1 (.node(Enable));
  _1BitDecoder u_1bitdecoder_2 (._0(\output [0]), ._1(\output [1]), .Bit(Input[0]), .Enable(n1bitdecoder_1__0));
  _1BitDecoder u_1bitdecoder_3 (._0(\output [2]), ._1(\output [3]), .Bit(Input[0]), .Enable(n1bitdecoder_1__1));
endmodule

// 3BitDec
module _3BitDecoder (
  input  [2:0] Input,
  input  Enable,
  output [7:0] \output 
);

  wire n1bitdecoder_1__0, n1bitdecoder_1__1;

  Pull_Resistor #(.pull(1)) pull_resistor_1 (.node(Enable));
  _1BitDecoder u_1bitdecoder_1 (._0(n1bitdecoder_1__0), ._1(n1bitdecoder_1__1), .Bit(Input[2]), .Enable(Enable));
  _2BitDecoder u_2bitdecoder_1 (.Input(Input[1:0]), .Enable(n1bitdecoder_1__0), .\output (\output [3:0]));
  _2BitDecoder u_2bitdecoder_2 (.Input(Input[1:0]), .Enable(n1bitdecoder_1__1), .\output (\output [7:4]));
endmodule

module CPU (
  input  RESET
);

  wire BRANCH, BRmux, Clock, IMM, IR_WE, mem_alu, Mem_st, MEMLOAD, MEMSTORE, n, not_1_out, NOT_JUMP,
       or_1_out, or_2_out, outump, p, PC_WE, RegFileWE, z;
  wire [1:0] ALU_sel;
  wire [3:0] DESTN, multiplexer_4_out, multiplexer_6_out, Src1_in, Src2_in;
  wire [4:0] BRANCH_ADDR;
  wire [7:0] IMM_Bits;
  wire [9:0] bit_extender_1_out, bit_extender_4_out;
  wire [11:0] LOAD_A;
  wire [15:0] outUMP_A;
  wire [19:0] ALUK, bit_extender_2_out, bit_extender_3_out, bit_extender_5_out, IMReg_Out, Memory,
       multiplexer_1_out, multiplexer_2_out, multiplexer_3_out, multiplexer_5_out, n20bitadder_1_output,
       n20bitadder_2_output, n20bitregister_1_output, rom_1_data, Src1_out, Src2_Out;

  // Probe on outUMP_A
  Bit_Extender #(.in_width(12), .out_width(10)) bit_extender_1 (.in(LOAD_A), .out(bit_extender_1_out));
  _20BitAdder u_20bitadder_1 (
    .input1(n20bitregister_1_output), .input2(multiplexer_2_out), .\output (n20bitadder_1_output));  // open: Cout
  // Probe on n20bitadder_1_output
  // Probe on bit_extender_1_out
  assign bit_extender_2_out = {{4{outUMP_A[15]}}, outUMP_A};  // Bit_Extender bit_extender_2
  assign bit_extender_3_out = {{15{BRANCH_ADDR[4]}}, BRANCH_ADDR};  // Bit_Extender bit_extender_3
  // Probe on BRANCH_ADDR
  or or_1 (or_1_out, outump, BRANCH);
  _20BitRegister u_20bitregister_1 (
    .AscSet0(RESET), .WE(PC_WE), .Input(n20bitadder_1_output), .\output (n20bitregister_1_output),
    .Clock(Clock));
  Multiplexer #(.width(20), .enable("false")) multiplexer_1 (
    .in0(bit_extender_2_out), .in1(bit_extender_3_out), .out(multiplexer_1_out), .sel(BRANCH));
  // Probe on n20bitregister_1_output
  // Probe on multiplexer_1_out
  Multiplexer #(.width(20), .enable("false")) multiplexer_2 (
    .in0(20'h1), .in1(n20bitadder_2_output), .out(multiplexer_2_out), .sel(or_1_out));
  // Probe on multiplexer_2_out
  Bit_Extender #(.in_width(20), .out_width(10)) bit_extender_4 (.in(n20bitregister_1_output), .out(bit_extender_4_out));
  RAM #(.addrWidth(10), .dataWidth(20), .bus("separate")) ram_1 (
    .addr(bit_extender_1_out), .din(Src1_out), .data(Memory), .str(MEMSTORE), .clk(Clock), .ld(MEMLOAD));  // open: sel, clr
  // Probe on Memory
  _20BitAdder u_20bitadder_2 (
    .input1(multiplexer_1_out), .input2(20'h1), .\output (n20bitadder_2_output));  // open: Cout
  // Probe on bit_extender_4_out
  // Probe on bit_extender_4_out
  // Probe on rom_1_data
  ROM #(.addrWidth(10), .dataWidth(20)) rom_1 (.addr(bit_extender_4_out), .data(rom_1_data));  // open: sel
  _20BitRegister u_20bitregister_2 (
    .WE(IR_WE), .Input(rom_1_data), .\output (IMReg_Out), .Clock(Clock));  // open: AscSet0
  Control_Unit control_unit_1 (
    .outump(outump), .MemoryStore(MEMSTORE), .MemoryLoad(MEMLOAD), .IMM_Signal(IMM), .Dst(DESTN),
    .Src1(Src1_in), .Src2(Src2_in), .outMPADDR(outUMP_A), .LDADDR(LOAD_A), .Instruction(IMReg_Out), .p(p),
    .z(z), .n(n), .IMM(IMM_Bits), .branch_address(BRANCH_ADDR), .IR_WE(IR_WE), .PC_WE(PC_WE),
    .ALU_control(ALU_sel), .Mem_alu(mem_alu), .Clock(Clock), .not_Jump(NOT_JUMP), .Branch_Sig(BRANCH),
    .Mem_st(Mem_st), .Branchmux(BRmux), .Operation2(Src2_Out), .Operation1(Src1_out), .RegFileWE(RegFileWE));
  // Probe on IMReg_Out
  // Probe on multiplexer_3_out
  // Probe on Src2_Out
  Multiplexer #(.width(20), .enable("false")) multiplexer_3 (
    .in0(ALUK), .in1(Memory), .out(multiplexer_3_out), .sel(mem_alu));
  // Probe on Src1_out
  RegisterFile registerfile_1 (
    .Clock(Clock), .Src2Addr(multiplexer_4_out), .Src1Addr(multiplexer_6_out), .DstAddr(DESTN),
    .Src2Out(Src2_Out), .Src1Out(Src1_out), .Input(multiplexer_3_out), .WE(RegFileWE));  // open: AscSet0
  // Probe on DESTN
  // Probe on multiplexer_4_out
  Multiplexer #(.width(4), .enable("false")) multiplexer_4 (
    .in0(Src2_in), .in1(Src1_in), .out(multiplexer_4_out), .sel(BRmux));
  // Probe on multiplexer_6_out
  // Probe on IMM_Bits
  // Probe on multiplexer_5_out
  // Probe on bit_extender_5_out
  assign bit_extender_5_out = {{12{IMM_Bits[7]}}, IMM_Bits};  // Bit_Extender bit_extender_5
  not not_1 (not_1_out, IMM);
  Multiplexer #(.width(20), .enable("false")) multiplexer_5 (
    .in0(bit_extender_5_out), .in1(Src2_Out), .out(multiplexer_5_out), .sel(not_1_out));
  // Probe on ALU_sel
  Clock clock_1 (.out(Clock));
  Multiplexer #(.width(4), .enable("false")) multiplexer_6 (
    .in0(Src1_in), .in1(DESTN), .out(multiplexer_6_out), .sel(or_2_out));
  or or_2 (or_2_out, Mem_st, BRmux);
  // Probe on Src2_Out
  AritmaticLogicUnit aritmaticlogicunit_1 (
    .Input2(Src1_out), .Input1(multiplexer_5_out), .Select(ALU_sel), .Output(ALUK));
  // Probe on Src1_out
  // Probe on ALUK

  // Notes on the sheet:
  //   Data Memory
  //   Instruction Memory
  //   contents of rom_1 (hex, n*v repeats v):
  //   90000 91001 92002 3120 1430a 25430 36508 47650 57615 68760 7981e a1004 a2005 b5612 0 0 c1014 0 0
  //   d2111 0 0 e5616 0 0 f4316 0 0 8fffc
endmodule

// ALU
module AritmaticLogicUnit (
  input  [19:0] Input1,
  input  [1:0] Select,
  input  [19:0] Input2,
  output [19:0] Output
);

  wire n20bitadder_1_cout;
  wire [19:0] multiplexer_1_out, n20bitadder_1_output, n20bitand_1_output, n20bitor_1_output,
       n20bitxor_1_output;

  // Probe on Input1
  _20BitAdder u_20bitadder_1 (
    .input1(Input1), .input2(Input2), .\output (n20bitadder_1_output), .Cout(n20bitadder_1_cout));
  _20BitAnd u_20bitand_1 (.input1(Input1), .input2(Input2), .\output (n20bitand_1_output));
  _20BitOr u_20bitor_1 (.input1(Input1), .input2(Input2), .\output (n20bitor_1_output));
  _20BitXor u_20bitxor_1 (.input1(Input1), .input2(Input2), .\output (n20bitxor_1_output));
  Multiplexer #(.select(2), .width(20), .enable("false")) multiplexer_1 (
    .in0(n20bitadder_1_output), .in1(n20bitand_1_output), .in2(n20bitor_1_output), .in3(n20bitxor_1_output),
    .out(multiplexer_1_out), .sel(Select));
  Bit_Extender #(.in_width(20), .out_width(20)) bit_extender_1 (.in(multiplexer_1_out), .out(Output));
endmodule

module RegisterFile (
  input  Clock,
  input  [3:0] Src2Addr,
  input  [3:0] Src1Addr,
  input  [3:0] DstAddr,
  input  AscSet0,
  input  WE,
  input  [19:0] Input,
  output [19:0] Src2Out,
  output [19:0] Src1Out
);

  wire _0, _1, _2, _3, _4, _5, _6, _7, _8, _9, _10, _11, _12, _13, _14, _15;
  wire [15:0] n4bitdecoder_1_output, n4bitdecoder_2_output;
  wire [19:0] n20bitregister_1_output, n20bitregister_2_output, n20bitregister_3_output,
       n20bitregister_4_output, n20bitregister_5_output, n20bitregister_6_output, n20bitregister_7_output,
       n20bitregister_8_output, n20bitregister_9_output, n20bitregister_10_output, n20bitregister_11_output,
       n20bitregister_12_output, n20bitregister_13_output, n20bitregister_14_output,
       n20bitregister_15_output, n20bitregister_16_output;

  _4BitDecoder u_4bitdecoder_1 (.\output (n4bitdecoder_1_output), .Input(Src1Addr));  // open: Enable
  _20BitRegister u_20bitregister_1 (
    .AscSet0(AscSet0), .WE(_1), .Input(Input), .\output (n20bitregister_1_output), .Clock(Clock));
  _20BitRegister u_20bitregister_2 (
    .AscSet0(AscSet0), .WE(_3), .Input(Input), .\output (n20bitregister_2_output), .Clock(Clock));
  _20BitRegister u_20bitregister_3 (
    .AscSet0(AscSet0), .WE(_5), .Input(Input), .\output (n20bitregister_3_output), .Clock(Clock));
  _20BitRegister u_20bitregister_4 (
    .AscSet0(AscSet0), .WE(_7), .Input(Input), .\output (n20bitregister_4_output), .Clock(Clock));
  _20BitRegister u_20bitregister_5 (
    .AscSet0(AscSet0), .WE(_9), .Input(Input), .\output (n20bitregister_5_output), .Clock(Clock));
  _20BitRegister u_20bitregister_6 (
    .AscSet0(AscSet0), .WE(_11), .Input(Input), .\output (n20bitregister_6_output), .Clock(Clock));
  _20BitRegister u_20bitregister_7 (
    .AscSet0(AscSet0), .WE(_13), .Input(Input), .\output (n20bitregister_7_output), .Clock(Clock));
  _20BitRegister u_20bitregister_8 (
    .AscSet0(AscSet0), .WE(_15), .Input(Input), .\output (n20bitregister_8_output), .Clock(Clock));
  assign Src2Out = n4bitdecoder_2_output[1] ? n20bitregister_1_output : 20'bz;  // Controlled_Buffer controlled_buffer_1
  assign Src1Out = n4bitdecoder_1_output[1] ? n20bitregister_1_output : 20'bz;  // Controlled_Buffer controlled_buffer_2
  assign Src2Out = n4bitdecoder_2_output[3] ? n20bitregister_2_output : 20'bz;  // Controlled_Buffer controlled_buffer_3
  assign Src1Out = n4bitdecoder_1_output[3] ? n20bitregister_2_output : 20'bz;  // Controlled_Buffer controlled_buffer_4
  assign Src2Out = n4bitdecoder_2_output[5] ? n20bitregister_3_output : 20'bz;  // Controlled_Buffer controlled_buffer_5
  assign Src1Out = n4bitdecoder_1_output[5] ? n20bitregister_3_output : 20'bz;  // Controlled_Buffer controlled_buffer_6
  assign Src2Out = n4bitdecoder_2_output[7] ? n20bitregister_4_output : 20'bz;  // Controlled_Buffer controlled_buffer_7
  assign Src1Out = n4bitdecoder_1_output[7] ? n20bitregister_4_output : 20'bz;  // Controlled_Buffer controlled_buffer_8
  assign Src2Out = n4bitdecoder_2_output[9] ? n20bitregister_5_output : 20'bz;  // Controlled_Buffer controlled_buffer_9
  assign Src1Out = n4bitdecoder_1_output[9] ? n20bitregister_5_output : 20'bz;  // Controlled_Buffer controlled_buffer_10
  assign Src2Out = n4bitdecoder_2_output[11] ? n20bitregister_6_output : 20'bz;  // Controlled_Buffer controlled_buffer_11
  assign Src1Out = n4bitdecoder_1_output[11] ? n20bitregister_6_output : 20'bz;  // Controlled_Buffer controlled_buffer_12
  assign Src2Out = n4bitdecoder_2_output[13] ? n20bitregister_7_output : 20'bz;  // Controlled_Buffer controlled_buffer_13
  assign Src1Out = n4bitdecoder_1_output[13] ? n20bitregister_7_output : 20'bz;  // Controlled_Buffer controlled_buffer_14
  assign Src2Out = n4bitdecoder_2_output[15] ? n20bitregister_8_output : 20'bz;  // Controlled_Buffer controlled_buffer_15
  assign Src1Out = n4bitdecoder_1_output[15] ? n20bitregister_8_output : 20'bz;  // Controlled_Buffer controlled_buffer_16
  _20BitRegister u_20bitregister_9 (
    .AscSet0(AscSet0), .WE(_0), .Input(Input), .\output (n20bitregister_9_output), .Clock(Clock));
  _20BitRegister u_20bitregister_10 (
    .AscSet0(AscSet0), .WE(_2), .Input(Input), .\output (n20bitregister_10_output), .Clock(Clock));
  _20BitRegister u_20bitregister_11 (
    .AscSet0(AscSet0), .WE(_4), .Input(Input), .\output (n20bitregister_11_output), .Clock(Clock));
  _20BitRegister u_20bitregister_12 (
    .AscSet0(AscSet0), .WE(_6), .Input(Input), .\output (n20bitregister_12_output), .Clock(Clock));
  _20BitRegister u_20bitregister_13 (
    .AscSet0(AscSet0), .WE(_8), .Input(Input), .\output (n20bitregister_13_output), .Clock(Clock));
  _20BitRegister u_20bitregister_14 (
    .AscSet0(AscSet0), .WE(_10), .Input(Input), .\output (n20bitregister_14_output), .Clock(Clock));
  _20BitRegister u_20bitregister_15 (
    .AscSet0(AscSet0), .WE(_12), .Input(Input), .\output (n20bitregister_15_output), .Clock(Clock));
  _20BitRegister u_20bitregister_16 (
    .AscSet0(AscSet0), .WE(_14), .Input(Input), .\output (n20bitregister_16_output), .Clock(Clock));
  assign Src2Out = n4bitdecoder_2_output[0] ? n20bitregister_9_output : 20'bz;  // Controlled_Buffer controlled_buffer_17
  assign Src1Out = n4bitdecoder_1_output[0] ? n20bitregister_9_output : 20'bz;  // Controlled_Buffer controlled_buffer_18
  assign Src2Out = n4bitdecoder_2_output[2] ? n20bitregister_10_output : 20'bz;  // Controlled_Buffer controlled_buffer_19
  assign Src1Out = n4bitdecoder_1_output[2] ? n20bitregister_10_output : 20'bz;  // Controlled_Buffer controlled_buffer_20
  assign Src2Out = n4bitdecoder_2_output[4] ? n20bitregister_11_output : 20'bz;  // Controlled_Buffer controlled_buffer_21
  assign Src1Out = n4bitdecoder_1_output[4] ? n20bitregister_11_output : 20'bz;  // Controlled_Buffer controlled_buffer_22
  assign Src2Out = n4bitdecoder_2_output[6] ? n20bitregister_12_output : 20'bz;  // Controlled_Buffer controlled_buffer_23
  assign Src1Out = n4bitdecoder_1_output[6] ? n20bitregister_12_output : 20'bz;  // Controlled_Buffer controlled_buffer_24
  assign Src2Out = n4bitdecoder_2_output[8] ? n20bitregister_13_output : 20'bz;  // Controlled_Buffer controlled_buffer_25
  assign Src1Out = n4bitdecoder_1_output[8] ? n20bitregister_13_output : 20'bz;  // Controlled_Buffer controlled_buffer_26
  assign Src2Out = n4bitdecoder_2_output[10] ? n20bitregister_14_output : 20'bz;  // Controlled_Buffer controlled_buffer_27
  assign Src1Out = n4bitdecoder_1_output[10] ? n20bitregister_14_output : 20'bz;  // Controlled_Buffer controlled_buffer_28
  assign Src2Out = n4bitdecoder_2_output[12] ? n20bitregister_15_output : 20'bz;  // Controlled_Buffer controlled_buffer_29
  assign Src1Out = n4bitdecoder_1_output[12] ? n20bitregister_15_output : 20'bz;  // Controlled_Buffer controlled_buffer_30
  assign Src2Out = n4bitdecoder_2_output[14] ? n20bitregister_16_output : 20'bz;  // Controlled_Buffer controlled_buffer_31
  assign Src1Out = n4bitdecoder_1_output[14] ? n20bitregister_16_output : 20'bz;  // Controlled_Buffer controlled_buffer_32
  _4BitDecoder u_4bitdecoder_2 (.\output (n4bitdecoder_2_output), .Input(Src2Addr));  // open: Enable
  _4BitDecoder u_4bitdecoder_3 (
    .Enable(WE), .\output ({_15, _14, _13, _12, _11, _10, _9, _8, _7, _6, _5, _4, _3, _2, _1, _0}),
    .Input(DstAddr));

  // Other names for the same wires on the sheet: Src1[19:0] = Src1Out; Src2[19:0] = Src2Out
endmodule

module Control_Unit (
  input  Clock,
  input  [19:0] Instruction,
  input  [19:0] Operation1,
  input  [19:0] Operation2,
  output IR_WE,
  output PC_WE,
  output [3:0] Dst,
  output [3:0] Src1,
  output [3:0] Src2,
  output [15:0] outMPADDR,
  output [11:0] LDADDR,
  output [1:0] ALU_control,
  output p,
  output z,
  output n,
  output [7:0] IMM,
  output [4:0] branch_address,
  output Branchmux,
  output Branch_Sig,
  output Mem_st,
  output outump,
  output not_Jump,
  output MemoryStore,
  output RegFileWE,
  output MemoryLoad,
  output Mem_alu,
  output IMM_Signal
);

  wire ADD, ADDI, AND, and_1_out, and_2_out, and_3_out, and_4_out, and_5_out, ANDI, BEQ, BGE, BGT, BLE, BLT,
       Equal, GE, Greater, LE, Less, not_3_out, OR, ORI, XOR, XORI;

  Comparator #(.width(20)) comparator_1 ();  // open: a, b, gt, eq, lt
  _20BitComparator u_20bitcomparator_1 (.A(Operation1), .B(Operation2), .Greater(Greater), .Equal(Equal), .Less(Less));
  or u_IMM (IMM_Signal, XORI, ORI, ANDI, ADDI);
  not not_1 (not_Jump, outump);
  or or_1 (GE, Greater, Equal);
  or or_2 (Mem_alu, Mem_st, MemoryLoad);
  or or_3 (LE, Less, Equal);
  and and_1 (and_1_out, BEQ, Equal);
  and and_2 (and_2_out, BGE, GE);
  and and_3 (and_3_out, BLE, LE);
  and and_4 (and_4_out, BLT, Less);
  and and_5 (and_5_out, BGT, Greater);
  or Art (RegFileWE, XOR, AND, OR, ADD, Mem_st, MemoryLoad, XORI, ORI, ANDI, ADDI);
  or or_4 (Branch_Sig, and_1_out, and_2_out, and_3_out, and_4_out, and_5_out);
  not not_2 (IR_WE, PC_WE);
  or or_5 (Branchmux, BEQ, BGE, BLE, BLT, BGT);
  _4BitDecoder u_4bitdecoder_1 (
    .\output ({BGE, BLE, BGT, BLT, BEQ, Mem_st, MemoryLoad, outump, XORI, XOR, ORI, OR, ANDI, AND, ADDI, ADD}),
    .Input(Instruction[19:16]));  // open: Enable
  D_Flip_Flop_part d_ff_1 (.clk(Clock), .D(not_3_out), .Q(PC_WE));  // open: Qn, preset, en, reset
  not not_3 (not_3_out, PC_WE);

  assign ALU_control = Instruction[18:17];
  assign branch_address = Instruction[7:3];
  assign Dst = Instruction[15:12];
  assign IMM = Instruction[7:0];
  assign LDADDR = Instruction[11:0];
  assign MemoryStore = Mem_st;
  assign n = Instruction[0];
  assign outMPADDR = Instruction[15:0];
  assign p = Instruction[2];
  assign Src1 = Instruction[11:8];
  assign Src2 = Instruction[7:4];
  assign z = Instruction[1];

  // Other names for the same wires on the sheet: LD = MemoryLoad; ST = Mem_st; Op1[3:0] = Instruction[15:12];
  //   Op2[3:0] = Instruction[11:8]; OpCode[3:0] = Instruction[19:16]; S = PC_WE
endmodule

// 4BitDec
module _4BitDecoder (
  input  [3:0] Input,
  input  Enable,
  output [15:0] \output 
);

  wire n1bitdecoder_1__0, n1bitdecoder_1__1;

  Pull_Resistor #(.pull(1)) pull_resistor_1 (.node(Enable));
  _1BitDecoder u_1bitdecoder_1 (._0(n1bitdecoder_1__0), ._1(n1bitdecoder_1__1), .Bit(Input[3]), .Enable(Enable));
  _3BitDecoder u_3bitdecoder_1 (.Enable(n1bitdecoder_1__0), .\output (\output [7:0]), .Input(Input[2:0]));
  _3BitDecoder u_3bitdecoder_2 (.Enable(n1bitdecoder_1__1), .\output (\output [15:8]), .Input(Input[2:0]));
endmodule

// 2-1Mux
module _1BitMux (
  input  i0,
  input  Select,
  input  Enable,
  input  i1,
  output Output
);

  wire and_1_out, and_2_out, n1bitdecoder_1__0, n1bitdecoder_1__1;

  Pull_Resistor #(.pull(1)) pull_resistor_1 (.node(Enable));
  _1BitDecoder u_1bitdecoder_1 (._0(n1bitdecoder_1__0), ._1(n1bitdecoder_1__1), .Bit(Select), .Enable(Enable));
  and and_1 (and_1_out, n1bitdecoder_1__0, i0);
  and and_2 (and_2_out, i1, n1bitdecoder_1__1);
  or or_1 (Output, and_1_out, and_2_out);
endmodule

// 4-1Mux
module _2BitMux (
  input  [1:0] Select,
  input  Enable,
  input  i0,
  input  i1,
  input  i2,
  input  i3,
  output Output
);

  wire n1bitdecoder_1__0, n1bitdecoder_1__1, n1bitmux_1_output, n1bitmux_2_output;

  Pull_Resistor #(.pull(1)) pull_resistor_1 (.node(Enable));
  _1BitDecoder u_1bitdecoder_1 (._0(n1bitdecoder_1__0), ._1(n1bitdecoder_1__1), .Bit(Select[1]), .Enable(Enable));
  _1BitMux u_1bitmux_1 (.Enable(n1bitdecoder_1__0), .i0(i0), .i1(i1), .Output(n1bitmux_1_output), .Select(Select[0]));
  _1BitMux u_1bitmux_2 (.Enable(n1bitdecoder_1__1), .i0(i2), .i1(i3), .Output(n1bitmux_2_output), .Select(Select[0]));
  or or_1 (Output, n1bitmux_1_output, n1bitmux_2_output);
endmodule

// BitAdder
module _1BitAdder (
  input  _1stBit,
  input  Cin,
  input  _2ndBit,
  output Sum,
  output Cout
);

  wire and_1_out, and_2_out, and_3_out, and_4_out, not_1_out, xnor_1_out;

  xnor xnor_1 (xnor_1_out, Cin, _2ndBit);
  not not_1 (not_1_out, xnor_1_out);
  and and_1 (and_1_out, _1stBit, xnor_1_out);
  and and_2 (and_2_out, ~_1stBit, not_1_out);  // AND_Gate
  and and_3 (and_3_out, not_1_out, _1stBit);
  and and_4 (and_4_out, Cin, _2ndBit);
  or or_1 (Sum, and_1_out, and_2_out);
  or or_2 (Cout, and_3_out, and_4_out);
endmodule

// Xor
module _20BitXor (
  input  [19:0] input1,
  input  [19:0] input2,
  output [19:0] \output 
);

  xor xor_1 (\output [10], input1[10], input2[10]);
  xor xor_2 (\output [11], input1[11], input2[11]);
  xor xor_3 (\output [12], input1[12], input2[12]);
  xor xor_4 (\output [13], input1[13], input2[13]);
  xor xor_5 (\output [14], input1[14], input2[14]);
  xor xor_6 (\output [15], input1[15], input2[15]);
  xor xor_7 (\output [16], input1[16], input2[16]);
  xor xor_8 (\output [17], input1[17], input2[17]);
  xor xor_9 (\output [18], input1[18], input2[18]);
  xor xor_10 (\output [19], input1[19], input2[19]);
  xor xor_11 (\output [0], input1[0], input2[0]);
  xor xor_12 (\output [1], input1[1], input2[1]);
  xor xor_13 (\output [2], input1[2], input2[2]);
  xor xor_14 (\output [3], input1[3], input2[3]);
  xor xor_15 (\output [4], input1[4], input2[4]);
  xor xor_16 (\output [5], input1[5], input2[5]);
  xor xor_17 (\output [6], input1[6], input2[6]);
  xor xor_18 (\output [7], input1[7], input2[7]);
  xor xor_19 (\output [8], input1[8], input2[8]);
  xor xor_20 (\output [9], input1[9], input2[9]);

  // Other names for the same wires on the sheet: i1[19:0] = input1; i2[19:0] = input2; _2[9:0] = \output [9:0];
  //   _1[9:0] = \output [19:10]
endmodule

// Adder
module _20BitAdder (
  input  [19:0] input2,
  input  [19:0] input1,
  output [19:0] \output ,
  output Cout
);

  wire n1bitadder_1_cout, n1bitadder_2_cout, n1bitadder_3_cout, n1bitadder_4_cout, n1bitadder_5_cout,
       n1bitadder_6_cout, n1bitadder_7_cout, n1bitadder_8_cout, n1bitadder_9_cout, n1bitadder_10_cout,
       n1bitadder_11_cout, n1bitadder_12_cout, n1bitadder_13_cout, n1bitadder_14_cout, n1bitadder_15_cout,
       n1bitadder_16_cout, n1bitadder_17_cout, n1bitadder_18_cout, n1bitadder_19_cout;

  _1BitAdder u_1bitadder_1 (
    .Cin(1'b0), ._2ndBit(input1[0]), .Sum(\output [0]), .Cout(n1bitadder_1_cout), ._1stBit(input2[0]));
  _1BitAdder u_1bitadder_2 (
    .Cin(n1bitadder_1_cout), ._2ndBit(input1[1]), .Sum(\output [1]), .Cout(n1bitadder_2_cout),
    ._1stBit(input2[1]));
  _1BitAdder u_1bitadder_3 (
    .Cin(n1bitadder_2_cout), ._2ndBit(input1[2]), .Sum(\output [2]), .Cout(n1bitadder_3_cout),
    ._1stBit(input2[2]));
  _1BitAdder u_1bitadder_4 (
    .Cin(n1bitadder_3_cout), ._2ndBit(input1[3]), .Sum(\output [3]), .Cout(n1bitadder_4_cout),
    ._1stBit(input2[3]));
  _1BitAdder u_1bitadder_5 (
    .Cin(n1bitadder_4_cout), ._2ndBit(input1[4]), .Sum(\output [4]), .Cout(n1bitadder_5_cout),
    ._1stBit(input2[4]));
  _1BitAdder u_1bitadder_6 (
    .Cin(n1bitadder_5_cout), ._2ndBit(input1[5]), .Sum(\output [5]), .Cout(n1bitadder_6_cout),
    ._1stBit(input2[5]));
  _1BitAdder u_1bitadder_7 (
    .Cin(n1bitadder_6_cout), ._2ndBit(input1[6]), .Sum(\output [6]), .Cout(n1bitadder_7_cout),
    ._1stBit(input2[6]));
  _1BitAdder u_1bitadder_8 (
    .Cin(n1bitadder_7_cout), ._2ndBit(input1[7]), .Sum(\output [7]), .Cout(n1bitadder_8_cout),
    ._1stBit(input2[7]));
  _1BitAdder u_1bitadder_9 (
    .Cin(n1bitadder_8_cout), ._2ndBit(input1[8]), .Sum(\output [8]), .Cout(n1bitadder_9_cout),
    ._1stBit(input2[8]));
  _1BitAdder u_1bitadder_10 (
    .Cin(n1bitadder_9_cout), ._2ndBit(input1[9]), .Sum(\output [9]), .Cout(n1bitadder_10_cout),
    ._1stBit(input2[9]));
  _1BitAdder u_1bitadder_11 (
    .Cin(n1bitadder_10_cout), ._2ndBit(input1[10]), .Sum(\output [10]), .Cout(n1bitadder_11_cout),
    ._1stBit(input2[10]));
  _1BitAdder u_1bitadder_12 (
    .Cin(n1bitadder_11_cout), ._2ndBit(input1[11]), .Sum(\output [11]), .Cout(n1bitadder_12_cout),
    ._1stBit(input2[11]));
  _1BitAdder u_1bitadder_13 (
    .Cin(n1bitadder_12_cout), ._2ndBit(input1[12]), .Sum(\output [12]), .Cout(n1bitadder_13_cout),
    ._1stBit(input2[12]));
  _1BitAdder u_1bitadder_14 (
    .Cin(n1bitadder_13_cout), ._2ndBit(input1[13]), .Sum(\output [13]), .Cout(n1bitadder_14_cout),
    ._1stBit(input2[13]));
  _1BitAdder u_1bitadder_15 (
    .Cin(n1bitadder_14_cout), ._2ndBit(input1[14]), .Sum(\output [14]), .Cout(n1bitadder_15_cout),
    ._1stBit(input2[14]));
  _1BitAdder u_1bitadder_16 (
    .Cin(n1bitadder_15_cout), ._2ndBit(input1[15]), .Sum(\output [15]), .Cout(n1bitadder_16_cout),
    ._1stBit(input2[15]));
  _1BitAdder u_1bitadder_17 (
    .Cin(n1bitadder_16_cout), ._2ndBit(input1[16]), .Sum(\output [16]), .Cout(n1bitadder_17_cout),
    ._1stBit(input2[16]));
  _1BitAdder u_1bitadder_18 (
    .Cin(n1bitadder_17_cout), ._2ndBit(input1[17]), .Sum(\output [17]), .Cout(n1bitadder_18_cout),
    ._1stBit(input2[17]));
  _1BitAdder u_1bitadder_19 (
    .Cin(n1bitadder_18_cout), ._2ndBit(input1[18]), .Sum(\output [18]), .Cout(n1bitadder_19_cout),
    ._1stBit(input2[18]));
  _1BitAdder u_1bitadder_20 (
    .Cin(n1bitadder_19_cout), ._2ndBit(input1[19]), .Sum(\output [19]), .Cout(Cout), ._1stBit(input2[19]));
endmodule

// And
module _20BitAnd (
  input  [19:0] input1,
  input  [19:0] input2,
  output [19:0] \output 
);

  and and_1 (\output [10], input1[10], input2[10]);
  and and_2 (\output [11], input1[11], input2[11]);
  and and_3 (\output [12], input1[12], input2[12]);
  and and_4 (\output [13], input1[13], input2[13]);
  and and_5 (\output [14], input1[14], input2[14]);
  and and_6 (\output [15], input1[15], input2[15]);
  and and_7 (\output [16], input1[16], input2[16]);
  and and_8 (\output [17], input1[17], input2[17]);
  and and_9 (\output [18], input1[18], input2[18]);
  and and_10 (\output [19], input1[19], input2[19]);
  and and_11 (\output [0], input1[0], input2[0]);
  and and_12 (\output [1], input1[1], input2[1]);
  and and_13 (\output [2], input1[2], input2[2]);
  and and_14 (\output [3], input1[3], input2[3]);
  and and_15 (\output [4], input1[4], input2[4]);
  and and_16 (\output [5], input1[5], input2[5]);
  and and_17 (\output [6], input1[6], input2[6]);
  and and_18 (\output [7], input1[7], input2[7]);
  and and_19 (\output [8], input1[8], input2[8]);
  and and_20 (\output [9], input1[9], input2[9]);

  // Other names for the same wires on the sheet: i1[19:0] = input1; i2[19:0] = input2; _2[9:0] = \output [9:0];
  //   _1[9:0] = \output [19:10]
endmodule

// Or
module _20BitOr (
  input  [19:0] input1,
  input  [19:0] input2,
  output [19:0] \output 
);

  or or_1 (\output [10], input1[10], input2[10]);
  or or_2 (\output [11], input1[11], input2[11]);
  or or_3 (\output [12], input1[12], input2[12]);
  or or_4 (\output [13], input1[13], input2[13]);
  or or_5 (\output [14], input1[14], input2[14]);
  or or_6 (\output [15], input1[15], input2[15]);
  or or_7 (\output [16], input1[16], input2[16]);
  or or_8 (\output [17], input1[17], input2[17]);
  or or_9 (\output [18], input1[18], input2[18]);
  or or_10 (\output [19], input1[19], input2[19]);
  or or_11 (\output [0], input1[0], input2[0]);
  or or_12 (\output [1], input1[1], input2[1]);
  or or_13 (\output [2], input1[2], input2[2]);
  or or_14 (\output [3], input1[3], input2[3]);
  or or_15 (\output [4], input1[4], input2[4]);
  or or_16 (\output [5], input1[5], input2[5]);
  or or_17 (\output [6], input1[6], input2[6]);
  or or_18 (\output [7], input1[7], input2[7]);
  or or_19 (\output [8], input1[8], input2[8]);
  or or_20 (\output [9], input1[9], input2[9]);

  // Other names for the same wires on the sheet: i1[19:0] = input1; i2[19:0] = input2; _2[9:0] = \output [9:0];
  //   _1[9:0] = \output [19:10]
endmodule

// Equal
module _20BitEqual (
  input  [19:0] input2,
  input  [19:0] input1,
  output \output 
);

  wire [19:0] xnor_1_out;

  assign xnor_1_out = ~(input1 ^ input2);  // XNOR_Gate xnor_1, 20 bits wide
  and and_1 (\output , xnor_1_out[0], xnor_1_out[1], xnor_1_out[2], xnor_1_out[3], xnor_1_out[4], xnor_1_out[5], xnor_1_out[6], xnor_1_out[7], xnor_1_out[8], xnor_1_out[9], xnor_1_out[10], xnor_1_out[11], xnor_1_out[12], xnor_1_out[13], xnor_1_out[14], xnor_1_out[15], xnor_1_out[16], xnor_1_out[17], xnor_1_out[18], xnor_1_out[19]);
endmodule

// 20-BitRegister
module _20BitRegister (
  input  [19:0] Input,
  input  Clock,
  input  WE,
  input  AscSet0,
  output [19:0] \output 
);

  D_Flip_Flop_part d_ff_1 (.clk(Clock), .D(Input[9]), .Q(\output [9]), .en(WE), .reset(AscSet0));  // open: Qn, preset
  Pull_Resistor pull_resistor_1 (.node(AscSet0));
  D_Flip_Flop_part d_ff_2 (.clk(Clock), .D(Input[19]), .Q(\output [19]), .en(WE), .reset(AscSet0));  // open: Qn, preset
  D_Flip_Flop_part d_ff_3 (.clk(Clock), .D(Input[8]), .Q(\output [8]), .en(WE), .reset(AscSet0));  // open: Qn, preset
  D_Flip_Flop_part d_ff_4 (.clk(Clock), .D(Input[18]), .Q(\output [18]), .en(WE), .reset(AscSet0));  // open: Qn, preset
  D_Flip_Flop_part d_ff_5 (.clk(Clock), .D(Input[7]), .Q(\output [7]), .en(WE), .reset(AscSet0));  // open: Qn, preset
  D_Flip_Flop_part d_ff_6 (.clk(Clock), .D(Input[17]), .Q(\output [17]), .en(WE), .reset(AscSet0));  // open: Qn, preset
  D_Flip_Flop_part d_ff_7 (.clk(Clock), .D(Input[6]), .Q(\output [6]), .en(WE), .reset(AscSet0));  // open: Qn, preset
  D_Flip_Flop_part d_ff_8 (.clk(Clock), .D(Input[16]), .Q(\output [16]), .en(WE), .reset(AscSet0));  // open: Qn, preset
  D_Flip_Flop_part d_ff_9 (.clk(Clock), .D(Input[5]), .Q(\output [5]), .en(WE), .reset(AscSet0));  // open: Qn, preset
  D_Flip_Flop_part d_ff_10 (
    .clk(Clock), .D(Input[15]), .Q(\output [15]), .en(WE), .reset(AscSet0));  // open: Qn, preset
  D_Flip_Flop_part d_ff_11 (.clk(Clock), .D(Input[4]), .Q(\output [4]), .en(WE), .reset(AscSet0));  // open: Qn, preset
  D_Flip_Flop_part d_ff_12 (
    .clk(Clock), .D(Input[14]), .Q(\output [14]), .en(WE), .reset(AscSet0));  // open: Qn, preset
  D_Flip_Flop_part d_ff_13 (.clk(Clock), .D(Input[3]), .Q(\output [3]), .en(WE), .reset(AscSet0));  // open: Qn, preset
  D_Flip_Flop_part d_ff_14 (
    .clk(Clock), .D(Input[13]), .Q(\output [13]), .en(WE), .reset(AscSet0));  // open: Qn, preset
  D_Flip_Flop_part d_ff_15 (.clk(Clock), .D(Input[2]), .Q(\output [2]), .en(WE), .reset(AscSet0));  // open: Qn, preset
  D_Flip_Flop_part d_ff_16 (
    .clk(Clock), .D(Input[12]), .Q(\output [12]), .en(WE), .reset(AscSet0));  // open: Qn, preset
  D_Flip_Flop_part d_ff_17 (.clk(Clock), .D(Input[1]), .Q(\output [1]), .en(WE), .reset(AscSet0));  // open: Qn, preset
  D_Flip_Flop_part d_ff_18 (
    .clk(Clock), .D(Input[11]), .Q(\output [11]), .en(WE), .reset(AscSet0));  // open: Qn, preset
  D_Flip_Flop_part d_ff_19 (.clk(Clock), .D(Input[0]), .Q(\output [0]), .en(WE), .reset(AscSet0));  // open: Qn, preset
  D_Flip_Flop_part d_ff_20 (
    .clk(Clock), .D(Input[10]), .Q(\output [10]), .en(WE), .reset(AscSet0));  // open: Qn, preset

  // Other names for the same wires on the sheet: in0 = Input[0]; in1 = Input[1]; in2 = Input[2]; in3 = Input[3];
  //   in4 = Input[4]; in5 = Input[5]; in6 = Input[6]; in7 = Input[7]; in8 = Input[8]; in9 = Input[9];
  //   in10 = Input[10]; in11 = Input[11]; in12 = Input[12]; in13 = Input[13]; in14 = Input[14]; in15 = Input[15];
  //   in16 = Input[16]; in17 = Input[17]; in18 = Input[18]; in19 = Input[19]; out0 = \output [0]; out1 = \output [1];
  //   out2 = \output [2]; out3 = \output [3]; out4 = \output [4]; out5 = \output [5]; out6 = \output [6];
  //   out7 = \output [7]; out8 = \output [8]; out9 = \output [9]; out10 = \output [10]; out11 = \output [11];
  //   out12 = \output [12]; out13 = \output [13]; out14 = \output [14]; out15 = \output [15]; out16 = \output [16];
  //   out17 = \output [17]; out18 = \output [18]; out19 = \output [19]
endmodule

module _20BitGreater (
  input  [1:0] in_1,
  input  [1:0] in_2,
  input  [1:0] in_3,
  input  [1:0] in_4,
  output out_5,
  output out_6,
  output out_7,
  output [1:0] out_8,
  output out_9
);

  wire undriven_3;
  wire [2:0] undriven_2;
  wire [7:0] shifter_1_out, undriven;

  Shifter shifter_1 (.in(undriven), .\dist (undriven_2), .out(shifter_1_out));
  Comparator #(.width(2)) comparator_1 (.a(in_1), .b(in_2), .gt(out_5), .eq(out_6), .lt(out_7));
  Subtractor #(.width(2)) subtractor_1 (.a(in_3), .b(in_4), .out(out_8), .bin(undriven_3), .bout(out_9));
endmodule

module _4BitComparator (
  input  A3,
  input  B3,
  input  A2,
  input  B2,
  input  A_B,
  input  A_B_2,
  input  A_B_3,
  input  A1,
  input  B1,
  input  A0,
  input  B0,
  output A_B_4,
  output A_B_5,
  output A_B_6
);

  wire and_1_out, and_2_out, and_3_out, and_4_out, and_5_out, and_6_out, and_7_out, and_8_out, and_9_out,
       and_10_out, and_11_out, and_12_out, and_13_out, and_14_out, and_15_out, and_16_out, and_17_out,
       and_18_out, and_19_out, and_20_out, nand_1_out, nand_2_out, nand_3_out, nand_4_out, nor_1_out,
       nor_2_out, nor_3_out, nor_4_out;

  nand nand_1 (nand_1_out, A2, B2);
  nand nand_2 (nand_2_out, A1, B1);
  nand nand_3 (nand_3_out, A0, B0);
  nand nand_4 (nand_4_out, A3, B3);
  and and_1 (and_1_out, A3, nand_4_out);
  and and_2 (and_2_out, nand_4_out, B3);
  and and_3 (and_3_out, A2, nand_1_out);
  and and_4 (and_4_out, nand_1_out, B2);
  and and_5 (and_5_out, A1, nand_2_out);
  and and_6 (and_6_out, nand_2_out, B1);
  and and_7 (and_7_out, A0, nand_3_out);
  and and_8 (and_8_out, nand_3_out, B0);
  nor nor_1 (nor_1_out, and_1_out, and_2_out);
  nor nor_2 (nor_2_out, and_3_out, and_4_out);
  nor nor_3 (nor_3_out, and_5_out, and_6_out);
  nor nor_4 (nor_4_out, and_7_out, and_8_out);
  and and_9 (and_9_out, B3, nand_4_out);
  and and_10 (and_10_out, B2, nand_1_out, nor_1_out);
  and and_11 (and_11_out, B1, nand_2_out, nor_1_out, nor_2_out);
  and and_12 (and_12_out, B0, nand_3_out, nor_1_out, nor_2_out, nor_3_out);
  and and_13 (and_13_out, nor_1_out, nor_2_out, nor_3_out, nor_4_out, A_B);
  and and_14 (and_14_out, nor_1_out, nor_2_out, nor_3_out, nor_4_out, A_B_2);
  and and_15 (and_15_out, A_B_2, nor_4_out, nor_3_out, nor_2_out, nor_1_out);
  and and_16 (and_16_out, A_B_3, nor_4_out, nor_2_out, nor_3_out, nor_1_out);
  and and_17 (and_17_out, nor_3_out, nor_2_out, nor_1_out, nand_3_out, A0);
  and and_18 (and_18_out, nor_2_out, nor_1_out, nand_2_out, A1);
  and and_19 (and_19_out, nor_1_out, nand_1_out, A2);
  and and_20 (and_20_out, nand_4_out, A3);
  nor nor_5 (A_B_4, and_9_out, and_10_out, and_11_out, and_12_out, and_13_out, and_14_out);
  and and_21 (A_B_5, nor_1_out, nor_2_out, A_B_2, nor_3_out, nor_4_out);
  nor nor_6 (A_B_6, and_15_out, and_16_out, and_17_out, and_18_out, and_19_out, and_20_out);
endmodule

module _8BitComparator (
  input  A7,
  input  A6,
  input  A5,
  input  A4,
  input  A3,
  input  A2,
  input  A1,
  input  A0,
  input  A_B,
  input  A_B_2,
  input  A_B_3,
  input  B7,
  input  B6,
  input  B5,
  input  B4,
  input  B3,
  input  B2,
  input  B1,
  input  B0,
  output A_B_4,
  output A_B_5,
  output A_B_6
);

  wire n4bitcomparator_1_a_b_4, n4bitcomparator_1_a_b_5, n4bitcomparator_1_a_b_6;

  _4BitComparator u_4bitcomparator_1 (
    .A3(A3), .B3(B3), .A2(A2), .B2(B2), .A_B(A_B), .A_B_2(A_B_2), .A_B_3(A_B_3), .A1(A1), .B1(B1), .A0(A0),
    .B0(B0), .A_B_4(n4bitcomparator_1_a_b_4), .A_B_5(n4bitcomparator_1_a_b_5), .A_B_6(n4bitcomparator_1_a_b_6));
  _4BitComparator u_4bitcomparator_2 (
    .A3(A7), .B3(B7), .A2(A6), .B2(B6), .A_B(n4bitcomparator_1_a_b_6), .A_B_2(n4bitcomparator_1_a_b_5),
    .A_B_3(n4bitcomparator_1_a_b_4), .A1(A5), .B1(B5), .A0(A4), .B0(B4), .A_B_4(A_B_4), .A_B_5(A_B_5),
    .A_B_6(A_B_6));

  // Notes on the sheet:
  //   0
  //   1
  //   0
endmodule

module _20BitComparator (
  input  [19:0] A,
  input  [19:0] B,
  output Greater,
  output Equal,
  output Less
);

  wire e1, e2, g1, g2, l1, l2;

  // Probe on A
  // Probe on A
  // Probe on B
  _8BitComparator u_8bitcomparator_1 (
    .A7(A[7]), .A6(A[6]), .A5(A[5]), .A4(A[4]), .A3(A[3]), .A2(A[2]), .A1(A[1]), .A0(A[0]), .A_B(1'b0),
    .A_B_2(1'b1), .A_B_3(1'b0), .B7(B[7]), .B6(B[6]), .B5(B[5]), .B4(B[4]), .B3(B[3]), .B2(B[2]), .B1(B[1]),
    .B0(B[0]), .A_B_4(g1), .A_B_5(e1), .A_B_6(l1));
  // Probe on B
  _8BitComparator u_8bitcomparator_2 (
    .A7(A[15]), .A6(A[14]), .A5(A[13]), .A4(A[12]), .A3(A[11]), .A2(A[10]), .A1(A[9]), .A0(A[8]), .A_B(l1),
    .A_B_2(e1), .A_B_3(g1), .B7(B[15]), .B6(B[14]), .B5(B[13]), .B4(B[12]), .B3(B[11]), .B2(B[10]),
    .B1(B[9]), .B0(B[8]), .A_B_4(g2), .A_B_5(e2), .A_B_6(l2));
  _4BitComparator u_4bitcomparator_1 (
    .A3(A[19]), .B3(B[19]), .A2(A[18]), .B2(B[18]), .A_B(l2), .A_B_2(e2), .A_B_3(g2), .A1(A[17]), .B1(B[17]),
    .A0(A[16]), .B0(B[16]), .A_B_4(Greater), .A_B_5(Equal), .A_B_6(Less));

  // Other names for the same wires on the sheet: A1[7:0] = A[7:0]; A2[7:0] = A[15:8]; A3[3:0] = A[19:16];
  //   B1[7:0] = B[7:0]; B2[7:0] = B[15:8]; B3[3:0] = B[19:16]
endmodule
